# Fritzing sketch Untitled Sketch (saved by Fritzing 0.9.3b)
breadboards: 1

parts:
  Part1 = Arduino Ethernet Shield (Rev3)
  R1 = Resistor [tolerance=±5% resistance=220 package="0603 [SMD]"]
  S1 = Pushbutton [package=THT]

nets:
  N1: Part1.D2, R1.Pin_1, S1.leg1
  N2: Part1.5V, S1.leg0
  N3: Part1.GND, R1.Pin_0
