# Fritzing sketch Untitled Sketch (saved by Fritzing 0.9.3b)
breadboards: 1

parts:
  Part1 = Arduino Uno (Rev3)
  R1 = Resistor [tolerance=±5% resistance=220 package="0805 [SMD]"]
  part = SWITCH-MOMENTARY-2 [package=tactile-switch-1101ne]  # not connected
  part_2 = SWITCH-MOMENTARY-2 [package=tactile-switch-1101ne]  # not connected
  S1 = TILT-SWITCH-SW-200D [package=reed_switch_plastic]

nets:
  N1: Part1.D2, R1.Pin_1, S1.1
  N2: Part1.5V, S1.2
  N3: Part1.GND, R1.Pin_0
